# Fritzing sketch Tiny Tetris (saved by Fritzing 0.9.0b)

parts:
  Part1 = Pro Trinket 5V
  Part2 = PowerBoost 500 Charger
  S2 = Toggle Switch [package=THT]
  S3 = Pushbutton [package=THT]

nets:
  GND: Part1.GND, Part2.GND, S2.COM, S3.leg0
  N1: Part1.VBAT, Part2.5.0V
  N2: Part1.VBUS, Part2.USB
  N3: Part1.RESET, S3.leg1
  N4: Part2.ENABLE, S2.L1

notes:
  GND
  SCL
  SDA
  To 16x8 LED Matrix Backpack
  To Battery
  VCC
  Power Switch
  Reset Button

custom parts:
  Pro Trinket 5V: The Pro Trinket 5V is like an Arduino Pro Mini with more pins and USB included. Built with the common core Arduino chip, the ATmega328p, it has 18 GPIO, 2 extra analog inputs, 28K of flash, and 2K of RAM. It has onboard USB bootloading support with Optiboot support, so you can either program your Pro Trinket over USB or with a FTDI cable. The Pro Trinket is programmable using the Arduino IDE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
  PowerBoost 500 Charger: The PowerBoost 500C is a little DC/DC boost converter module that can be powered by any 3.7V LiIon/LiPoly battery, and convert the battery output to 5.2V DC for running your 5V projects. At its heart is a TPS61090 boost converter from TI. This boost converter chip has some really nice extras such as low battery detection, 2A internal switch, synchronous conversion, excellent efficiency, and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
